// Logisim project ex4.circ as structural Verilog: 5 circuits, main circuit RotRight
module RotRight (
  input  [15:0] INPUT0,
  input  [3:0] AMOUNT,
  output [15:0] OUTPUT0
);
endmodule

module rot1 (
  input  [15:0] in_1,
  output [15:0] out_2
);

  assign out_2 = {in_1[0], {15{1'b0}}} | {1'b0, in_1[15:1]};  // OR_Gate or_1, 16 bits wide
endmodule

module rot2 (
  input  [15:0] in_1,
  output [15:0] out_2
);

  assign out_2 = {in_1[15:14], {14{1'b0}}} | {2'b00, in_1[15:2]};  // OR_Gate or_1, 16 bits wide
endmodule

module rot4 (
  input  [15:0] in_1,
  output [15:0] out_2
);

  assign out_2 = {in_1[3:0], {12{1'b0}}} | {4'b0000, in_1[15:4]};  // OR_Gate or_1, 16 bits wide
endmodule

module rot8 (
  input  [15:0] in_1,
  output [15:0] out_2
);

  assign out_2 = {in_1[7:0], {8{1'b0}}} | {{8{1'b0}}, in_1[15:8]};  // OR_Gate or_1, 16 bits wide
endmodule
